// Logisim project FUCK_Final.circ as structural Verilog: 1 circuit, main circuit main
module main (
  input  in_1,
  input  [31:0] in_2,
  input  [31:0] in_3,
  input  [3:0] in_4,
  input  [4:0] in_5,
  input  [31:0] in_6,
  input  in_7,
  input  [4:0] in_8,
  input  [4:0] in_9,
  input  [4:0] in_10,
  output [31:0] out_11
);

  wire clock_1_out, clock_2_out, registerfile_1_p7, registerfile_1_p8, registerfile_2_p1, registerfile_2_p7,
       registerfile_2_p8;
  wire [4:0] risc_vprogramrom_1_p2_2, rom_1_data;
  wire [31:0] adder_1_out, register_1_q, risc_vprogramrom_1_p2;

  Clock clock_1 (.out(clock_1_out));
  Register #(.width(32)) register_1 (.D(adder_1_out), .clk(clock_1_out), .Q(register_1_q), .clr(in_1));  // open: en
  Adder #(.width(32)) adder_1 (.a(32'h4), .b(register_1_q), .out(adder_1_out));  // open: cin, cout
  // Probe on register_1_q
  Clock clock_2 (.out(clock_2_out));
  // ALU alu_1: pin names not known; wires that end beside it: in_2, in_3, in_4, in_5, out_11
  // RISC_VProgramROM risc_vprogramrom_1: pin names not known; wires that end beside it: register_1_q, {risc_vprogramrom_1_p2[31:20], risc_vprogramrom_1_p2_2, risc_vprogramrom_1_p2[14:0]}
  // Probe on registerfile_1_p7
  // RegisterFile registerfile_1: pin names not known; wires that end beside it: in_6, clock_2_out, in_7, in_8, in_9, in_10, registerfile_1_p7, registerfile_1_p8
  // Probe on {risc_vprogramrom_1_p2[31:20], risc_vprogramrom_1_p2_2, risc_vprogramrom_1_p2[14:0]}
  // Probe on risc_vprogramrom_1_p2[14:12]
  // Probe on registerfile_1_p8
  // Probe on risc_vprogramrom_1_p2[11:7]
  // Probe on risc_vprogramrom_1_p2_2
  // Probe on risc_vprogramrom_1_p2[31:25]
  ROM #(.addrWidth(10), .dataWidth(5)) rom_1 (
    .addr({risc_vprogramrom_1_p2[31:25], risc_vprogramrom_1_p2[14:12]}), .data(rom_1_data));
  // Probe on risc_vprogramrom_1_p2[24:20]
  // RegisterFile registerfile_2: pin names not known; wires that end beside it: registerfile_2_p1, clock_1_out, rom_1_data[4], risc_vprogramrom_1_p2[11:7], risc_vprogramrom_1_p2_2, risc_vprogramrom_1_p2[24:20], registerfile_2_p7, registerfile_2_p8
  // Probe on rom_1_data[3:0]
  // ALU alu_2: pin names not known; wires that end beside it: registerfile_2_p7, registerfile_2_p8, rom_1_data[3:0], registerfile_2_p1

  // Notes on the sheet:
  //   contents of risc_vprogramrom_1 (hex, n*v repeats v):
  //   add x2, x2, x1 add x2, x2, x1 add x2, x2, x1 add x2, x2, x1 add x2, x2, x1 add x2, x2, x1 add x2,
  //   x2, x1 add x2, x2, x1 add x2, x2, x1 add x2, x2, x1 add x2, x2, x1 add x2, x2, x1 add x2, x2, x1 add
  //   x2, x2, x1 add x2, x2, x1 add x2, x2, x1 add x2, x2, x1 add x2, x2, x1 add x2, x2, x1 add x2, x2, x1
  //   add x2, x2, x1 add x2, x2, x1 add x2, x2, x1 add x2, x2, x1 add x2, x2, x1 add x2, x2, x1 add x2,
  //   x2, x1 add x2, x2, x1 add x2, x2, x1 add x2, x2, x1 add x2, x2, x1 add x2, x2, x1 add x2, x2, x1 add
  //   x2, x2, x1 add x2, x2, x1 add x2, x2, x1 add x2, x2, x1 add x2, x2, x1 add x2, x2, x1 add x2, x2, x1
  //   add x2, x2, x1 add x2, x2, x1 add x2, x2, x1 add x2, x2, x1 add x2, x2, x1 add x2, x2, x1 add x2,
  //   x2, x1 add x2, x2, x1 add x2, x2, x1 add x2, x2, x1 add x2, x2, x1 add x2, x2, x1 add x2, x2, x1 add
  //   x2, x2, x1 add x2, x2, x1 add x2, x2, x1 add x2, x2, x1 add x2, x2, x1 add x2, x2, x1 add x2, x2, x1
  //   add x2, x2, x1 add x2, x2, x1 add x2, x2, x1 add x2, x2, x1 add x2, x2, x1 add x2, x2, x1 add x2,
  //   x2, x1 add x2, x2, x1 add x2, x2, x1 add x2, x2, x1 add x2, x2, x1 add x2, x2, x1 add x2, x2, x1 add
  //   x2, x2, x1 add x2, x2, x1 add x2, x2, x1 add x2, x2, x1 add x2, x2, x1 add x2, x2, x1 add x2, x2, x1
  //   add x2, x2, x1 add x2, x2, x1 add x2, x2, x1 add x2, x2, x1 add x2, x2, x1 add x2, x2, x1 add x2,
  //   x2, x1 add x2, x2, x1 add x2, x2, x1 add x2, x2, x1 add x2, x2, x1 add x2, x2, x1 add x2, x2, x1 add
  //   x2, x2, x1 add x2, x2, x1 add x2, x2, x1 add x2, x2, x1 add x2, x2, x1 add x2, x2, x1 add x2, x2, x1
  //   add x2, x2, x1 add x2, x2, x1 add x2, x2, x1 add x2, x2, x1 add x2, x2, x1 add x2, x2, x1 add x2,
  //   x2, x1 add x2, x2, x1 add x2, x2, x1 add x2, x2, x1 add x2, x2, x1 add x2, x2, x1 add x2, x2, x1 add
  //   x2, x2, x1 add x2, x2, x1 add x2, x2, x1 add x2, x2, x1 add x2, x2, x1 add x2, x2, x1 add x2, x2, x1
  //   add x2, x2, x1 add x2, x2, x1 add x2, x2, x1 add x2, x2, x1 add x2, x2, x1 add x2, x2, x1 add x2,
  //   x2, x1 add x2, x2, x1 add x2, x2, x1 add x2, x2, x1 add x2, x2, x1 add x2, x2, x1 add x2, x2, x1 add
  //   x2, x2, x1 add x2, x2, x1 add x2, x2, x1 add x2, x2, x1 add x2, x2, x1 add x2, x2, x1 add x2, x2, x1
  //   add x2, x2, x1 add x2, x2, x1 add x2, x2, x1 add x2, x2, x1 add x2, x2, x1 add x2, x2, x1 add x2,
  //   x2, x1 add x2, x2, x1 add x2, x2, x1 add x2, x2, x1 add x2, x2, x1 add x2, x2, x1 add x2, x2, x1 add
  //   x2, x2, x1 add x2, x2, x1 add x2, x2, x1 add x2, x2, x1 add x2, x2, x1 add x2, x2, x1 add x2, x2, x1
  //   add x2, x2, x1 add x2, x2, x1 add x2, x2, x1 add x2, x2, x1 add x2, x2, x1 add x2, x2, x1 add x2,
  //   x2, x1 add x2, x2, x1 add x2, x2, x1 add x2, x2, x1 add x2, x2, x1 add x2, x2, x1 add x2, x2, x1 add
  //   x2, x2, x1 add x2, x2, x1 add x2, x2, x1 add x2, x2, x1 add x2, x2, x1 add x2, x2, x1 add x2, x2, x1
  //   add x2, x2, x1 add x2, x2, x1 add x2, x2, x1 add x2, x2, x1 add x2, x2, x1 add x2, x2, x1 add x2,
  //   x2, x1 add x2, x2, x1 add x2, x2, x1 add x2, x2, x1 add x2, x2, x1 add x2, x2, x1 add x2, x2, x1 add
  //   x2, x2, x1 add x2, x2, x1 add x2, x2, x1 add x2, x2, x1 add x2, x2, x1 add x2, x2, x1 add x2, x2, x1
  //   add x2, x2, x1 add x2, x2, x1 add x2, x2, x1 add x2, x2, x1 add x2, x2, x1 add x2, x2, x1 add x2,
  //   x2, x1 add x2, x2, x1 add x2, x2, x1 add x2, x2, x1 add x2, x2, x1 add x2, x2, x1 add x2, x2, x1 add
  //   x2, x2, x1 add x2, x2, x1 add x2, x2, x1 add x2, x2, x1 add x2, x2, x1 add x2, x2, x1 add x2, x2, x1
  //   add x2, x2, x1 add x2, x2, x1 add x2, x2, x1 add x2, x2, x1 add x2, x2, x1 add x2, x2, x1 add x2,
  //   x2, x1 add x2, x2, x1 add x2, x2, x1 add x2, x2, x1 add x2, x2, x1 add x2, x2, x1 add x2, x2, x1 add
  //   x2, x2, x1 add x2, x2, x1 add x2, x2, x1 add x2, x2, x1 add x2, x2, x1 add x2, x2, x1 add x2, x2, x1
  //   add x2, x2, x1 add x2, x2, x1 add x2, x2, x1 add x2, x2, x1 add x2, x2, x1 add x2, x2, x1 add x2,
  //   x2, x1 add x2, x2, x1 add x2, x2, x1 add x2, x2, x1 add x2, x2, x1 add x2, x2, x1 add x2, x2, x1 add
  //   x2, x2, x1 add x2, x2, x1 add x2, x2, x1
  //   contents of rom_1 (hex, n*v repeats v):
  //   1f 251*0 1c 0 0 0 1c
endmodule
