// Logisim project HW_5_Datapath.circ as structural Verilog: 5 circuits, main circuit main
module main (
  input  in_1,
  input  in_2
);

  wire clock_1_out, control_1_bsel, control_1_immsel, control_1_we;
  wire [3:0] control_1_alusel;
  wire [6:0] risc_vprogramrom_1_p2;
  wire [24:0] risc_vprogramrom_1_p2_2;
  wire [31:0] adder_1_out, immgen_1_imm, multiplexer_1_out, register_1_q, registerfile_1_p1,
       registerfile_1_p7, registerfile_1_p8, slti_1_out_5, test_ram_1_dataout;

  Clock clock_1 (.out(clock_1_out));
  Register #(.width(32)) register_1 (.D(adder_1_out), .clk(clock_1_out), .Q(register_1_q), .clr(in_2));  // open: en
  Adder #(.width(32)) adder_1 (.a(32'h4), .b(register_1_q), .out(adder_1_out));  // open: cin, cout
  // Probe on register_1_q
  // RISC_VProgramROM risc_vprogramrom_1: pin names not known; wires that end beside it: register_1_q, {risc_vprogramrom_1_p2_2, risc_vprogramrom_1_p2}
  // Probe on {risc_vprogramrom_1_p2_2, risc_vprogramrom_1_p2}
  Control control_1 (
    .in_1({risc_vprogramrom_1_p2_2, risc_vprogramrom_1_p2}), .ALUSel(control_1_alusel),
    .BSel(control_1_bsel), .ImmSel(control_1_immsel), .WE(control_1_we));
  // Probe on risc_vprogramrom_1_p2_2[4:0]
  // Probe on risc_vprogramrom_1_p2_2[7:5]
  ImmGen immgen_1 (.Inst(risc_vprogramrom_1_p2_2), .ImmSel(control_1_immsel), .Imm(immgen_1_imm));
  // Probe on risc_vprogramrom_1_p2_2[12:8]
  // Probe on risc_vprogramrom_1_p2_2[24:18]
  // Probe on risc_vprogramrom_1_p2_2[17:13]
  // Probe on registerfile_1_p7
  // RegisterFile registerfile_1: pin names not known; wires that end beside it: registerfile_1_p1, clock_1_out, control_1_we, risc_vprogramrom_1_p2_2[4:0], risc_vprogramrom_1_p2_2[12:8], risc_vprogramrom_1_p2_2[17:13], registerfile_1_p7, registerfile_1_p8
  // Probe on immgen_1_imm
  // Probe on control_1_alusel
  Multiplexer #(.width(32), .enable("false")) multiplexer_1 (
    .in0(registerfile_1_p8), .in1(immgen_1_imm), .out(multiplexer_1_out), .sel(control_1_bsel));
  Slti slti_1 (
    .A(registerfile_1_p7), .B(multiplexer_1_out), .SA(multiplexer_1_out[4:0]), ._1010(control_1_alusel),
    .out_5(slti_1_out_5));
  Test_Ram test_ram_1 (
    .Address(slti_1_out_5[23:0]), .DataIn(registerfile_1_p8), .Clk(clock_1_out), .DataOut(test_ram_1_dataout));  // open: Clear, StoreWord, LoadWord, SelectBytes
  Multiplexer #(.width(32), .enable("false")) multiplexer_2 (
    .in0(slti_1_out_5), .in1(test_ram_1_dataout), .out(registerfile_1_p1), .sel(in_1));

  // Notes on the sheet:
  //   contents of risc_vprogramrom_1 (hex, n*v repeats v):
  //   addi x3,x3,1000  add x2,x3,x1  # slli x1,x1,2 # srli x1,x1,2 # xori x1,x3,1
endmodule

module ImmGen (
  input  [24:0] Inst,
  input  ImmSel,
  output [31:0] Imm
);

  wire [11:0] multiplexer_1_out;

  // Probe on Inst
  // Probe on Inst
  Multiplexer #(.width(12), .enable("false")) multiplexer_1 (
    .in0(Inst[24:13]), .in1({Inst[24:18], Inst[4:0]}), .out(multiplexer_1_out), .sel(ImmSel));
  assign Imm = {{20{multiplexer_1_out[11]}}, multiplexer_1_out};  // Bit_Extender bit_extender_1

  // Notes on the sheet:
  //   I-Type
  //   S-Type
endmodule

module Test_Ram (
  input  [23:0] Address,
  input  [31:0] DataIn,
  input  Clear,
  input  Clk,
  input  StoreWord,
  input  LoadWord,
  input  [3:0] SelectBytes,
  output [31:0] DataOut
);

  RAM #(.addrWidth(24)) ram_1 (
    .addr(Address), .data(DataOut[7:0]), .sel(SelectBytes[0]), .clk(Clk), .ld(LoadWord), .clr(Clear));
  // Pins of 8 and 32 bits meet at DataOut
  // Pins of 1 and 4 bits meet at SelectBytes
endmodule

module Control (
  input  [31:0] in_1,
  output [3:0] ALUSel,
  output BSel,
  output ImmSel,
  output WE
);

  wire undriven;
  wire [15:0] rom_1_data, rom_2_data;
  wire [15:7] multiplexer_1_out;

  ROM #(.addrWidth(10), .dataWidth(16)) rom_1 (.addr({in_1[14:12], in_1[6:0]}), .data(rom_1_data));
  ROM #(.addrWidth(17), .dataWidth(16)) rom_2 (.addr({in_1[31:25], in_1[14:12], in_1[6:0]}), .data(rom_2_data));
  ROM #(.addrWidth(17), .dataWidth(1)) rom_3 (.addr({in_1[31:25], in_1[14:12], in_1[6:0]}));  // open: data
  // Probe on undriven
  Multiplexer #(.width(16), .enable("false")) multiplexer_1 (
    .in0(rom_1_data), .in1(rom_2_data), .out({multiplexer_1_out, WE, ImmSel, BSel, ALUSel}), .sel(undriven));

  // Notes on the sheet:
  //   contents of rom_1 (hex, n*v repeats v):
  //   0 0 0 4f 15*0 5f 15*0 1 95*0 4f 127*0 4f 15*0 5a 127*0 55 127*0 54 127*0 56 127*0 51 127*0 50
  //   contents of rom_2 (hex, n*v repeats v):
  //   51*0 4f 95*0 53 31*0 43 127*0 4a 127*0 45 127*0 44 95*0 56 31*0 46 127*0 41 127*0 40 31871*0 4c
  //   607*0 57 31*0 47
  //   contents of rom_3 (hex, n*v repeats v):
  //   51*0 1 94*0 1 1 511*0 1 32767*0 1
  //   Don't Have funct7
  //   Have Funct 7
endmodule

module Slti (
  input  [31:0] A,
  input  [31:0] B,
  input  [4:0] SA,
  input  [3:0] _1010,
  output [31:0] out_5
);

  wire comparator_1_eq, comparator_2_eq, comparator_3_lt, comparator_4_lt, multiplexer_1_out, or_1_out;
  wire [31:0] alu_1_p5, bit_extender_1_out;

  Comparator #(.width(4)) comparator_1 (.a(_1010), .b(4'b1010), .eq(comparator_1_eq));  // open: gt, lt
  Comparator #(.width(4)) comparator_2 (.a(_1010), .b(4'b0101), .eq(comparator_2_eq));  // open: gt, lt
  Comparator #(.width(32)) comparator_3 (.a(A), .b(B), .lt(comparator_3_lt));  // open: gt, eq
  Comparator #(.width(32), .mode("unsigned")) comparator_4 (.a(A), .b(B), .lt(comparator_4_lt));  // open: gt, eq
  or or_1 (or_1_out, comparator_1_eq, comparator_2_eq);
  Multiplexer #(.enable("false")) multiplexer_1 (
    .in0(comparator_3_lt), .in1(comparator_4_lt), .out(multiplexer_1_out), .sel(comparator_2_eq));
  // ALU alu_1: pin names not known; wires that end beside it: A, B, _1010, SA, alu_1_p5
  assign bit_extender_1_out = {{31{1'b0}}, multiplexer_1_out};  // Bit_Extender bit_extender_1
  Multiplexer #(.width(32), .enable("false")) multiplexer_2 (
    .in0(alu_1_p5), .in1(bit_extender_1_out), .out(out_5), .sel(or_1_out));

  // Notes on the sheet:
  //   0101
endmodule
